# Fritzing sketch Schematic Arduino Mega Final (saved by Fritzing 0.9.9b)

parts:
  L298N1 = L298N DC motor driver
  U1 = LIPO-2000mAh [package=lipo-2000]
  M1 = DC Motor
  M6 = RioRand LM2596
  U2 = POT [package=pot_alpha_rv16af-20]
  A1 = UPS control board lipo to 12V
  M7 = DC Motor
  J2 = Basic Servo
  BAT1 = Battery Holders [package=battery-aa-kit]
  A2 = X9C103S module
  M11 = DC Motor  # not connected
  M12 = RioRand LM2596
  L298N2 = L298N DC motor driver
  DC1 = DC_DC_XL4016 [package=board_screw]
  A3 = 400w dc-dc constant current boost converter
  Part3 = InvenSense MPU6050
  JACK1 = 2.1mm Barrel Jack with Terminal Block
  J3 = KF142R-5.08-3P [package="Clamp Terminal Bloc"]
  J4 = KF142R-5.08-3P [package="Clamp Terminal Bloc"]
  J5 = KF142R-5.08-3P [package="Clamp Terminal Bloc"]
  J6 = KF142R-5.08-3P [package="Clamp Terminal Bloc"]
  J7 = KF142R-5.08-3P [package="Clamp Terminal Bloc"]
  Mod1 = KY-003 Hall Magnetic Sensor Module [package="Breakout board"]
  J8 = KF142R-5.08-3P [package="Clamp Terminal Bloc"]
  J9 = KF142R-5.08-3P [package="Clamp Terminal Bloc"]
  J12 = KF142R-5.08-3P [package="Clamp Terminal Bloc"]
  J13 = KF142R-5.08-3P [package="Clamp Terminal Bloc"]
  J14 = KF142R-5.08-3P [package="Clamp Terminal Bloc"]
  J15 = KF142R-5.08-3P [package="Clamp Terminal Bloc"]
  J16 = KF142R-5.08-3P [package="Clamp Terminal Bloc"]
  J18 = KF142R-5.08-3P [package="Clamp Terminal Bloc"]
  J19 = KF142R-5.08-3P [package="Clamp Terminal Bloc"]
  J20 = KF142R-5.08-3P [package="Clamp Terminal Bloc"]
  J21 = KF142R-5.08-3P [package="Clamp Terminal Bloc"]
  U4 = LuaNode32 / ESP32 [part_number=ESP32S-PIN30]
  Part5 = Arduino Mega ADK (Rev3)
  J22 = KF142R-5.08-3P [package="Clamp Terminal Bloc"]
  J23 = KF142R-5.08-3P [package="Clamp Terminal Bloc"]
  J24 = female pin header, 2 pins [form="♀ (female)"]  # not connected
  J26 = KF142R-5.08-3P [package="Clamp Terminal Bloc"]
  J27 = KF142R-5.08-3P [package="Clamp Terminal Bloc"]
  J28 = KF142R-5.08-3P [package="Clamp Terminal Bloc"]
  J29 = KF142R-5.08-3P [package="Clamp Terminal Bloc"]
  RY3 = SSR-40VA
  Part10 = Voltage Sensor 25V
  Part13 = ACS712 Current Sensor Module
  RY4 = SSR-40VA
  S2 = Toggle Switch spst [package=THT]
  S3 = Toggle Switch spst [package=THT]
  RY5 = SSR-40VA
  F1 = Fan - Ventilador [package=THT]
  F2 = Fan - Ventilador [package=THT]
  J30 = KF142R-5.08-3P [package="Clamp Terminal Bloc"]
  J31 = KF142R-5.08-3P [package="Clamp Terminal Bloc"]
  U5 = LM2596 step down module

nets:
  N1: L298N1.OUT3, M1.pin_2
  N2: L298N1.OUT4, RY3.Pin_2
  N3: L298N1.12V, J18.pin2, J18.pin_5
  N4: L298N1.GND, J21.pin2, J21.pin_5
  N5: L298N1.ENB, A2.Pin_6
  N6: L298N1.IN3, A2.Pin_8
  N7: L298N1.IN4, A2.Pin_7
  N8: U1.+, S2.L1
  N9: U1.-, J21.pin1, J21.pin_4
  N10: M1.pin_1, RY3.Pin_1
  N11: M6.Pin_1, M7.pin_2
  N12: M6.Pin_2, M7.pin_1
  N13: M6.Pin_3, J13.pin3, J13.pin_6
  N14: M6.Pin_4, J16.pin1, J16.pin_4
  N15: U2.A, J6.pin2, J6.pin_5
  N16: U2.S, Part5.A0
  N17: U2.E, J4.pin_4
  N18: A1.Pin_1, J8.pin3, J8.pin_6
  N19: A1.Pin_5, J9.pin3, J9.pin_6
  N20: A1.Pin_6, BAT1.+
  N21: A1.Pin_7, BAT1.-
  N22: A1.Pin_8, J23.pin2, J23.pin_5
  N23: A1.Pin_9, S3.L1
  N24: J2.gnd, J12.pin3, J12.pin_6
  N25: J2.vcc, M12.Pin_3
  N26: J2.pulse, Part5.D11_PWM
  N27: A2.Pin_1, J7.pin3, J7.pin_6
  N28: A2.Pin_2, Part5.D10_PWM
  N29: A2.Pin_3, Part5.D8_PWM
  N30: A2.Pin_4, Part5.D9_PWM
  N31: A2.Pin_5, J5.pin_5
  N32: M12.Pin_1, J13.pin2, J13.pin_5
  N33: M12.Pin_2, J16.pin2, J16.pin_5
  N34: M12.Pin_4, J12.pin2, J12.pin_5
  N35: L298N2.12V, J8.pin2, J8.pin_5
  N36: L298N2.GND, J28.pin3, J28.pin_6
  N37: L298N2.IN3, Part5.D6_PWM
  N38: L298N2.IN4, Part5.D5_PWM
  N39: DC1.IN+, J18.pin1, J18.pin_4
  N40: DC1.IN-, J21.pin3, J21.pin_6
  N41: DC1.OUT+, J9.pin1, J9.pin_4
  N42: DC1.OUT-, J8.pin1, J8.pin_4
  N43: A3.Pin_1, Part13.INPUT+
  N44: A3.Pin_2, A3.Pin_3, J16.pin_6, J20.pin1, J20.pin_4
  N45: A3.Pin_4, RY5.Pin_2
  VCC: Part3.VCC, Part5.3V3
  GND: Part3.GND, J3.pin3, J3.pin_6, U4.GND, Part5.GND, J23.pin1, J23.pin_4, RY4.Pin_4, U5.IN-, U5.OUT-
  N46: Part3.SCL, Part5.D21/SCL
  N47: Part3.SDA, Part5.D20/SDA
  N48: JACK1.POS, J22.pin_6
  N49: JACK1.NEG, J23.pin3, J23.pin_6
  N50: J3.pin1, J3.pin_4, J12.pin1, J12.pin_4
  N51: J3.pin2, J3.pin_5, RY5.Pin_4
  N52: J4.pin_6, J28.pin1
  N53: J5.pin_4, J26.pin1, J26.pin_4
  N54: J5.pin_6, Mod1.-
  N55: J6.pin1, J6.pin_4, Mod1.Vin
  N56: J6.pin3, J6.pin_6, Part5.5V, J27.pin1, J27.pin_4
  N57: Mod1.S, Part5.D2_PWM
  N58: J9.pin2, J9.pin_5, J28.pin2, J28.pin_5
  N59: J13.pin_4, Part13.INPUT-
  N60: J14.pin_6, J27.pin_6, Part10.VCC, Part10.+
  N61: J15.pin_4, Part10.GND
  N62: J18.pin3, J18.pin_6, S2.COM
  N63: J19.pin_6, RY5.Pin_1
  N64: U4.VN, U4.TX0, Part5.D1/TX0
  N65: U4.Vin, U5.OUT+
  N66: U4.RX0, Part5.D0/RX0
  N67: Part5.A1, Part13.OUT
  N68: Part5.A2, Part10.S
  N69: Part5.D3_PWM, RY3.Pin_3
  N70: Part5.D4_PWM, RY5.Pin_3
  N71: Part5.D7_PWM, RY4.Pin_3
  N72: J22.pin1, U5.IN+
  N73: J22.pin_5, S3.COM
  N74: J26.pin2, J26.pin_5, Part13.GND
  N75: J26.pin_6, Part10.-
  N76: J27.pin2, J27.pin_5, Part13.VCC
  N77: J29.pin_6, RY3.Pin_4
  N78: F1.5V, J30.pin1
  N79: F1.GND, J31.pin1, J31.pin_4
  N80: F2.5V, J30.pin_5
  N81: F2.GND, J31.pin2, J31.pin_5

notes:
  Driver Motor 36V
  Baterie 36V
  Motor Electric 36V
  Magnetou MT
  Servomotor Viteza Motor Termic
  Ambreiaj
  Maneta Viteza
  Redresor&Regulator Tensiune MT 12V
  Regulator 36-->12V 4A
  Regulator 12-->42V
  Regulator 12-->6V 2.5A
  Baterie Backup 18650 3.7V
  Driver Motor 12V
  E-Switch Incarcare
  Terminal comun 12V
  Terminal comun   GND
  Terminale comune 5V GND ->
  Terminale comune 12V GND
  Digipot
  MPU6050
  KY-003
  Arduino Mega
  Terminale comune 36V GND
  ESP32
  Senzor Curent
  E-Switch Cheie Motor Termic
  Modul LM2596
  E-Switch Motor Electric
  Senzor Tensiune
  Terminale comune 5V GND
  Terminale comune     9V GND

custom parts:
  L298N DC motor driver: 2x DC motor driver with 78M05 positive voltage regulator (7..35 V) L298N: max 46 V, 2 A Set 5 V Enable jumper to enable 5 V regultor (needed for the L298N) and +5 V output at screw terminal or supply external +5 V at screw terminal Set ENA and/or ENB to +5 V to enable motor permanently or supply ENA and/or ENB with PWM signal IN1 and IN2 set rotation directory for motor A (OUT1/OUT2) IN2 and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
  UPS control board lipo to 12V: It is a UPS uninterruptible power supply control board.
  X9C103S module: Digital Potentiometer Module X9C103S Voltage Regulator Electronic For Arduino .
  400w dc-dc constant current boost converter: 400w dc-dc constant current boost converter.
  KF142R-5.08-3P: 5.08mm 14 ~ 22 awg 15A Trou traversant 250V 4 Push-Pull, P = 5.08mm Système de serrage à ressort Bornier ROHS
  KY-003 Hall Magnetic Sensor Module: KEYES KY-003 Arduino Hall Magnetic Sensor Module is a switch that will turn on/off in the presence of a magnetic field.
  LuaNode32 / ESP32: New Image for LuaNode32 DOIT ESP32 DEVKIT V1. Base parts from LuaNode32 / ESP32 ESP32 based LuaNode32 by G.Noorlander DOIT Esp32 DevKit v1 (30 pins long, 11 pins width) by Werner Rothschopf (modified by vanepp Dec 2018)
  SSR-40VA: SSR-40VA solid state relay.
  Toggle Switch spst: Toggle Switch single pole single throw
  Fan - Ventilador: Ventilador de 2 pines, se encuentra comunmente en computadoras de escritorio
  LM2596 step down module: LM2596 DC-DC step down power supply module 3 A.
